// Logisim project ALU.circ as structural Verilog: 3 circuits, main circuit main
module main (
  input  [31:0] A,
  input  [31:0] in_2,
  input  [31:0] B,
  input  [3:0] OPERATION,
  output PF,
  output ZF,
  output NF,
  output EQUAL,
  output [31:0] HI
);

  wire and_2_out, comparator_1_lt, comparator_2_lt;
  wire [31:0] ADD, AND, HI_DIV, HI_DIVU, HI_MUL, HI_MULU, LO_DIV, LO_DIVU, LO_MUL, LO_MULU, NOR, OR, S_LESS,
       SUB, U_LESS, XOR;

  MULU mulu_1 (.A(A), .B(B), .LO(LO_MULU), .HI(HI_MULU));
  DIV div_1 (.A(A), .B(B), .LO(LO_DIV), .HI(HI_DIV));
  Multiplier #(.width(32)) multiplier_1 (.a(A), .b(B), .out(LO_MUL), .cout(HI_MUL));  // open: cin
  Divider #(.width(32)) divider_1 (.a(A), .b(B), .out(LO_DIVU), .rem(HI_DIVU));  // open: upper
  Adder #(.width(32)) adder_1 (.a(A), .b(B), .out(ADD));  // open: cin, cout
  Subtractor #(.width(32)) subtractor_1 (.a(A), .b(B), .out(SUB));  // open: bin, bout
  Comparator #(.width(32)) comparator_1 (.a(A), .b(B), .eq(EQUAL), .lt(comparator_1_lt));  // open: gt
  assign S_LESS = {{31{1'b0}}, comparator_1_lt};  // Bit_Extender bit_extender_1
  Comparator #(.width(32)) comparator_2 (.a(A), .b(B), .lt(comparator_2_lt));  // open: gt, eq
  assign U_LESS = {{31{1'b0}}, comparator_2_lt};  // Bit_Extender bit_extender_2
  assign AND = A & B;  // AND_Gate and_1, 32 bits wide
  assign OR = A | B;  // OR_Gate or_1, 32 bits wide
  assign XOR = A ^ B;  // XOR_Gate xor_1, 32 bits wide
  assign NOR = ~(A | B);  // NOR_Gate nor_1, 32 bits wide
  Multiplexer #(.select(4), .width(32), .disabled(0), .enable("false")) multiplexer_1 (
    .in0({32{1'b0}}), .in1(A), .in2(S_LESS), .in3(U_LESS), .in4(LO_MUL), .in5(LO_MULU), .in6(LO_DIV),
    .in7(LO_DIVU), .in8(ADD), .in9(SUB), .in10(AND), .in11(OR), .in12(NOR), .in13(XOR), .out(in_2),
    .sel(OPERATION));  // open: in14, in15
  Multiplexer #(.select(2), .width(32)) multiplexer_2 (
    .in0(HI_MUL), .in1(HI_MULU), .in2(HI_DIV), .in3(HI_DIVU), .out(HI), .sel(OPERATION[1:0]), .en(and_2_out));
  Comparator #(.width(32)) comparator_3 (.a(in_2), .b({32{1'b0}}), .gt(PF), .eq(ZF), .lt(NF));
  and and_2 (and_2_out, OPERATION[2], ~OPERATION[3]);  // AND_Gate

  // Other names for the same wires on the sheet: OP[3:0] = OPERATION
endmodule

// +X
module MULU (
  input  [31:0] A,
  input  [31:0] B,
  output [31:0] LO,
  output [31:0] HI
);

  wire [31:0] adder_1_out, multiplexer_1_out, multiplexer_2_out, multiplier_1_cout;

  Multiplexer #(.width(32), .enable("false")) multiplexer_1 (
    .in0({32{1'b0}}), .in1(A), .out(multiplexer_1_out), .sel(B[31]));
  Multiplexer #(.width(32), .enable("false")) multiplexer_2 (
    .in0({32{1'b0}}), .in1(B), .out(multiplexer_2_out), .sel(A[31]));
  Multiplier #(.width(32)) multiplier_1 (.a(A), .b(B), .out(LO), .cout(multiplier_1_cout));  // open: cin
  Adder #(.width(32)) adder_1 (.a(multiplexer_1_out), .b(multiplexer_2_out), .out(adder_1_out));  // open: cin, cout
  Adder #(.width(32)) adder_2 (.a(multiplier_1_cout), .b(adder_1_out), .out(HI));  // open: cin, cout

  // Notes on the sheet:
  //   INPUTS
  //   MULU
  //   OUTPUTS
endmodule

module DIV (
  input  [31:0] A,
  input  [31:0] LO,
  input  [31:0] HI,
  input  [31:0] B
);

  wire xor_1_out;
  wire [31:0] divider_1_out, multiplexer_1_out, multiplexer_2_out, negator_1_out, negator_2_out,
       negator_3_out;

  Negator #(.width(32)) negator_1 (.in(A), .out(negator_1_out));
  Negator #(.width(32)) negator_2 (.in(B), .out(negator_2_out));
  Multiplexer #(.width(32), .enable("false")) multiplexer_1 (
    .in0(A), .in1(negator_1_out), .out(multiplexer_1_out), .sel(A[31]));
  Multiplexer #(.width(32), .enable("false")) multiplexer_2 (
    .in0(B), .in1(negator_2_out), .out(multiplexer_2_out), .sel(B[31]));
  Divider #(.width(32)) divider_1 (
    .a(multiplexer_1_out), .b(multiplexer_2_out), .out(divider_1_out), .rem(HI));  // open: upper
  xor xor_1 (xor_1_out, A[31], B[31]);
  Negator #(.width(32)) negator_3 (.in(divider_1_out), .out(negator_3_out));
  Multiplexer #(.width(32), .enable("false")) multiplexer_3 (
    .in0(divider_1_out), .in1(negator_3_out), .out(LO), .sel(xor_1_out));

  // Notes on the sheet:
  //   DIV
endmodule
